// Logisim project circuitc.circ as structural Verilog: 2 circuits, main circuit main
module main (
  input  S3,
  input  S2,
  input  S1,
  input  S0,
  input  Correct,
  output R3,
  output R2,
  output R1,
  output R0
);

  wire Half_Adder_2_c, Half_Adder_3_c, Half_Adder_4_c, xor_1_out, xor_2_out, xor_3_out, xor_4_out;

  Half_Adder Half_Adder (.a(xor_1_out), .b(Half_Adder_2_c), .s(R3));  // open: c
  xor xor_1 (xor_1_out, Correct, S3);
  Half_Adder Half_Adder_2 (.a(xor_2_out), .b(Half_Adder_3_c), .s(R2), .c(Half_Adder_2_c));
  xor xor_2 (xor_2_out, Correct, S2);
  Half_Adder Half_Adder_3 (.a(xor_3_out), .b(Half_Adder_4_c), .s(R1), .c(Half_Adder_3_c));
  xor xor_3 (xor_3_out, Correct, S1);
  Half_Adder Half_Adder_4 (.a(xor_4_out), .b(Correct), .s(R0), .c(Half_Adder_4_c));
  xor xor_4 (xor_4_out, Correct, S0);

  // Notes on the sheet:
  //   a
  //   C
  //   S
  //   b
  //   a
  //   C
  //   b
  //   S
  //   a
  //   C
  //   b
  //   S
  //   a
  //   C
  //   b
  //   S
endmodule

module Half_Adder (
  input  a,
  input  b,
  output s,
  output c
);

  xor xor_1 (s, a, b);
  and and_1 (c, a, b);
endmodule
