// Logisim project circuitd.circ as structural Verilog: 1 circuit, main circuit main
module main (
  input  Op,
  input  C,
  output Correct
);

  wire and_1_out, and_2_out, not_1_out, not_2_out;

  not not_1 (not_1_out, Op);
  not not_2 (not_2_out, C);
  and and_1 (and_1_out, Op, not_2_out);
  and and_2 (and_2_out, not_1_out, C);
  or or_1 (Correct, and_1_out, and_2_out);
endmodule
