// Logisim project real.circ as structural Verilog: 1 circuit, main circuit main
module main (
  input  X,
  input  A4,
  input  B4,
  input  C,
  output X_2,
  output X_prime,
  output A4_2,
  output A4_prime,
  output B4_2,
  output B4_prime,
  output C_2,
  output C_prime,
  output Op,
  output R4,
  output OVERFLOW
);

  wire and_1_out, and_2_out, and_3_out, and_4_out, and_5_out, and_6_out, and_7_out, and_8_out, and_9_out,
       and_10_out, and_11_out;

  not not_1 (X_prime, X);
  not not_2 (A4_prime, A4);
  not not_3 (B4_prime, B4);
  not not_4 (C_prime, C);
  and and_1 (and_1_out, X_prime, A4, B4_prime);
  and and_2 (and_2_out, X_prime, A4_prime, B4);
  and and_3 (and_3_out, X, A4, B4);
  and and_4 (and_4_out, X, A4_prime, B4_prime);
  and and_5 (and_5_out, A4_prime, X_prime, B4);
  and and_6 (and_6_out, X, B4_prime, C_prime);
  and and_7 (and_7_out, A4, C);
  and and_8 (and_8_out, X_prime, A4_prime, B4_prime, C);
  and and_9 (and_9_out, X_prime, A4, B4, C);
  and and_10 (and_10_out, X, A4, B4_prime, C);
  and and_11 (and_11_out, X, A4_prime, B4, C);
  or or_1 (Op, and_1_out, and_2_out, and_3_out, and_4_out);
  or or_2 (R4, and_5_out, and_6_out, and_7_out);
  or or_3 (OVERFLOW, and_8_out, and_9_out, and_10_out, and_11_out);

  assign A4_2 = A4;
  assign B4_2 = B4;
  assign C_2 = C;
  assign X_2 = X;
endmodule
